# Fritzing sketch Clock4 schematic (saved by Fritzing 0.9.0b)
breadboards: 1

parts:
  Part1 = Arduino Pro Mini v13
  Part2 = Real Time Clock Module - DS1307 RTC Breakout Board [part_number=DS3231]
  U1 = CAPSENSE_PAD [package=capsense_pad]
  R1 = PHOTOCELL [package=photocell-kit]
  R2 = Resistor [tolerance=±5% resistance=10k package=THT]
  R3 = Resistor [tolerance=±5% resistance=4.7k package=THT]
  R4 = Resistor [tolerance=±5% resistance=4.7k package=THT]
  LED1 = LED - 5mm [color="Red (633nm)" package="5 mm [THT]"]
  R5 = Resistor [tolerance=±5% resistance=1M package=THT]
  R6 = Resistor [tolerance=±5% resistance=1M package=THT]
  U2 = CAPSENSE_PAD [package=capsense_pad]
  C1 = Ceramic Capacitor [capacitance=100pF package="100 mil [THT, multilayer]"]
  C2 = Ceramic Capacitor [capacitance=100pF package="100 mil [THT, multilayer]"]

nets:
  5V: Part1.VCC, Part2.5V, R1.P$1, R3.Pin_0, R4.Pin_0
  N1: Part1.A4, Part2.SDA
  N2: Part1.A5, Part2.SCL, R4.Pin_1
  GND: Part1.GND, Part2.GND, R2.Pin_1, C1.0, C2.0
  N3: Part1.A0, R1.P$2, R2.Pin_0
  N4: Part1.D10_PWM/SS, LED1.cathode
  N5: Part1.D6_PWM, R6.Pin_1, U2.RECEIVE, C1.1
  N6: Part1.D5_PWM, R5.Pin_0, R6.Pin_0
  N7: Part1.D4, U1.RECEIVE, R5.Pin_1, C2.1
